// Digital circuit divisao.dig as structural Verilog
module divisao (
  input  [7:0] AC,
  input  [7:0] N,
  input  clock,
  input  start,
  input  _1,
  output [7:0] AC_out,
  output [7:0] MQ_out
);

  Register #(.Bits(8)) RestoReg (.D(AC), .C(clock), .en(_1), .Q(AC_out));
  Register #(.Bits(8)) QuocReg (.D({8{1'b0}}), .C(clock), .en(_1), .Q(MQ_out));

  // Notes on the sheet:
  //   _1: default 1
endmodule
