// Digital circuit divisor8bits.dig as structural Verilog
module divisor8bits (
  input  [7:0] AC,
  input  [7:0] N,
  input  clock,
  input  start,
  input  _1,
  input  _1_2,
  output [7:0] AC_out,
  output [7:0] MQ_out,
  output ok,
  output c0,
  output c1,
  output c2,
  output c3,
  output c4,
  output c5,
  output c6,
  output c0_2,
  output c1_2,
  output c2_2,
  output c3_2,
  output c4_2,
  output c5_2,
  output c6_2,
  output c7
);

  wire subtrator8bots_1_p26;
  wire [7:0] multiplexer_1_out, multiplexer_3_out, somador8bits_1_p2, subtrator8bots_1_p27;

  Register #(.Bits(8)) RestoReg (.D(multiplexer_1_out), .C(clock), .en(_1), .Q(AC_out));
  Register #(.Bits(8)) QuocReg (.D(multiplexer_3_out), .C(clock), .en(_1), .Q(MQ_out));
  Multiplexer #(.Bits(8)) multiplexer_1 (.sel(start), .in_0(multiplexer_1_out), .in_1(AC), .out(multiplexer_1_out));
  Multiplexer #(.Bits(8)) multiplexer_2 (.sel(ok), .in_0(AC_out), .in_1(subtrator8bots_1_p27), .out(multiplexer_1_out));
  // subtrator8bots subtrator8bots_1: pin names not known; wires that end beside it: N, AC_out, N, AC_out, N, AC_out, N, AC_out, N, AC_out, N, AC_out, N, AC_out, N, AC_out, N, _1_2, c0, c1, c2, c3, c4, c5, c6, subtrator8bots_1_p26, subtrator8bots_1_p27
  not not_1 (ok, subtrator8bots_1_p26);
  Multiplexer #(.Bits(8)) multiplexer_3 (
    .in_0(MQ_out), .in_1(somador8bits_1_p2), .out(multiplexer_3_out));  // open: sel
  // somador8bits somador8bits_1: pin names not known; wires that end beside it: MQ_out, somador8bits_1_p2, c7, c6_2, c5_2, c4_2, c3_2, c2_2, c1_2, c0_2

  // Notes on the sheet:
  //   _1: default 1
  //   _1_2: default 1
endmodule
