// Digital circuit multiplicador3bits.dig as structural Verilog
module multiplicador3bits (
  input  a0,
  input  b0,
  input  a1,
  input  b0_2,
  input  a0_2,
  input  b1,
  input  a1_2,
  input  b1_2,
  input  a2,
  input  b0_3,
  input  a2_2,
  input  b1_3,
  input  a0_3,
  input  b2,
  input  a1_3,
  input  b2_2,
  input  a2_3,
  input  b2_3,
  output p0,
  output x1,
  output x2,
  output x3,
  output p1,
  output c1,
  output x4,
  output x5,
  output x6,
  output x7,
  output x8,
  output p2,
  output p3,
  output p4,
  output p5
);

  wire and_11_out, and_12_out, xor_1_out, xor_3_out, xor_4_out;

  and and_1 (p0, a0, b0);
  and and_2 (x1, a1, b0_2);
  and and_3 (x2, a0_2, b1);
  and and_4 (x3, a1_2, b1_2);
  and and_5 (x4, a2, b0_3);
  and and_6 (x5, a2_2, b1_3);
  and and_7 (x6, a0_3, b2);
  and and_8 (x7, a1_3, b2_2);
  and and_9 (x8, a2_3, b2_3);
  and and_10 (c1, x1, x2);
  and and_11 (and_11_out, x3, c1);
  xor xor_1 (xor_1_out, and_11_out, x5);
  xor xor_2 (p1, x1, x2);
  xor xor_3 (xor_3_out, c1, x3);
  and and_12 (and_12_out, and_11_out, x5);
  xor xor_4 (xor_4_out, xor_3_out, x4);
  xor xor_5 (p4, and_12_out, x8);
  xor xor_6 (p2, xor_4_out, x6);
  and and_13 (p5, and_12_out, x8);
  xor xor_7 (p3, xor_1_out, x7);
endmodule
