// Digital circuit multiplicador8bits.dig as structural Verilog
module multiplicador8bits (
  input  b0,
  input  a0,
  input  a1,
  input  a2,
  input  a3,
  input  a4,
  input  a5,
  input  a6,
  input  a7,
  input  b1,
  input  a0_2,
  input  a1_2,
  input  a2_2,
  input  a3_2,
  input  a4_2,
  input  a5_2,
  input  a6_2,
  input  a7_2,
  input  gnd,
  output c0,
  output c1,
  output c2,
  output c3,
  output c4,
  output c6,
  output c6_2,
  output c7,
  output cout
);

  wire and_1_out, and_2_out, and_3_out, and_4_out, and_5_out, and_6_out, and_7_out, and_8_out, and_9_out,
       and_10_out, and_11_out, and_12_out, and_13_out, and_14_out, and_15_out, and_16_out;

  and and_1 (and_1_out, b0, a2);
  and and_2 (and_2_out, b0, a3);
  and and_3 (and_3_out, b0, a4);
  and and_4 (and_4_out, b0, a5);
  and and_5 (and_5_out, b0, a6);
  and and_6 (and_6_out, b0, a7);
  and and_7 (and_7_out, b1, a5_2);
  and and_8 (and_8_out, b1, a6_2);
  and and_9 (and_9_out, b1, a7_2);
  and and_10 (and_10_out, b0, a0);
  and and_11 (and_11_out, b0, a1);
  and and_12 (and_12_out, b1, a0_2);
  and and_13 (and_13_out, b1, a1_2);
  and and_14 (and_14_out, b1, a2_2);
  and and_15 (and_15_out, b1, a3_2);
  and and_16 (and_16_out, b1, a4_2);
  // somador8bits somador8bits_1: pin names not known; wires that end beside it: and_10_out, and_12_out, and_11_out, and_13_out, and_1_out, and_14_out, and_2_out, and_15_out, and_3_out, and_16_out, and_4_out, and_7_out, and_5_out, cout, c7, c6_2, c6, c4, c3, c2, c1, c0, gnd, and_9_out, and_6_out
endmodule
