// Digital circuit somador1bit.dig as structural Verilog
module somador1bit (
  input  a0,
  input  a1,
  input  cin,
  output S,
  output cout
);

  wire and_1_out, and_2_out, and_3_out, xor_1_out;

  and and_1 (and_1_out, a0, a1);
  and and_2 (and_2_out, a0, cin);
  and and_3 (and_3_out, a1, cin);
  xor xor_1 (xor_1_out, a0, a1);
  xor xor_2 (S, xor_1_out, cin);
  or or_1 (cout, and_1_out, and_2_out, and_3_out);
endmodule
