// Digital circuit somador4.dig as structural Verilog
module somador4 (
  input  a0,
  input  b0,
  input  a1,
  input  b1,
  input  a2,
  input  b2,
  input  a3,
  input  b3,
  input  cin,
  output c0,
  output c1,
  output c2,
  output c3
);

  wire s0, s1, s2, s3;

  somador1bit somador1bit_1 (.a0(a0), .a1(b0), .cin(cin), .S(c0), .cout(s0));
  somador1bit somador1bit_2 (.a0(a1), .a1(b1), .cin(s0), .S(c1), .cout(s1));
  somador1bit somador1bit_3 (.a0(a2), .a1(b2), .cin(s1), .S(c2), .cout(s2));
  somador1bit somador1bit_4 (.a0(a3), .a1(b3), .cin(s2), .S(c3), .cout(s3));
endmodule
