// Digital circuit subtrator8bots.dig as structural Verilog
module subtrator8bots (
  input  a0,
  input  b0,
  input  a1,
  input  b1,
  input  a2,
  input  b2,
  input  a3,
  input  b3,
  input  a4,
  input  b4,
  input  a5,
  input  b5,
  input  a6,
  input  b6,
  input  a7,
  input  b7,
  input  sub,
  output c0,
  output c1,
  output c2,
  output c3,
  output c4,
  output c5,
  output c6,
  output c7,
  output cout
);

  wire xor_1_out, xor_2_out, xor_3_out, xor_4_out, xor_5_out, xor_6_out, xor_7_out, xor_8_out;

  xor xor_1 (xor_1_out, sub, b1);
  xor xor_2 (xor_2_out, sub, b2);
  xor xor_3 (xor_3_out, sub, b3);
  xor xor_4 (xor_4_out, sub, b4);
  xor xor_5 (xor_5_out, sub, b5);
  xor xor_6 (xor_6_out, sub, b6);
  xor xor_7 (xor_7_out, sub, b0);
  xor xor_8 (xor_8_out, sub, b7);
  // somador8bits somador8bits_1: pin names not known; wires that end beside it: a0, xor_7_out, a1, xor_1_out, a2, xor_2_out, a3, xor_3_out, a4, xor_4_out, a5, xor_5_out, a6, xor_6_out, a7, xor_8_out, sub, c0, c1, c2, c3, c4, c5, c6, c7, cout
endmodule
